# Fritzing sketch jumanji (saved by Fritzing 0.9.3b)

parts:
  DFRobot_DFPlayer_Mini1 = DFRobot DFPlayer Mini [part_number=DFR0299]
  Part1 = Arduino Nano (Rev3.0) (ICSP)
  PIR1 = PIR sensor
  PIR2 = PIR sensor
  R1 = Resistor [tolerance=±5% resistance=1k package="0805 [SMD]"]
  R2 = Resistor [tolerance=±5% resistance=1k package="0805 [SMD]"]
  TTP223B1 = TTP223B Capacitive Touch Sensor Module
  S1 = Reed switch [package=THT]
  SP1 = SPEAKER [package=pcb_mount_speaker]
  Part4 = Adafruit VL53L0X Time of Flight Distance Sensor [part_number="Adafruit #3317"]

nets:
  VCC: DFRobot_DFPlayer_Mini1.VCC, Part1.VIN, TTP223B1.VCC, Part4.VIN
  N1: DFRobot_DFPlayer_Mini1.RX, R1.Pin_0
  N2: DFRobot_DFPlayer_Mini1.TX, R2.Pin_0
  N3: DFRobot_DFPlayer_Mini1.SPK_1, SP1.-
  GND: DFRobot_DFPlayer_Mini1.GND-1, DFRobot_DFPlayer_Mini1.GND-2, Part1.GND, TTP223B1.GND, Part4.GND
  N4: DFRobot_DFPlayer_Mini1.SPK_2, SP1.+
  N5: Part1.D5, TTP223B1.SIG
  N6: Part1.D8, R2.Pin_1
  N7: Part1.D9, R1.Pin_1
  N8: Part1.D10, PIR2.SIG
  N9: Part1.D11/MOSI, PIR1.SIG
  N10: Part1.D12/MISO, S1.pin_2
  N11: Part1.A6, Part4.SCL
  N12: Part1.A5, Part4.SDA
  GND_2: PIR1.GND, PIR2.GND

custom parts:
  TTP223B Capacitive Touch Sensor Module: The TTP223B capacitive touch sensor module uses the TTP223B IC. The appropriate voltage is approximately 2 to 5.5 volts.
  Adafruit VL53L0X Time of Flight Distance Sensor: The VL53L0X is a Time of Flight distance sensor like no other you've used! The sensor contains a very tiny invisible laser source, and a matching sensor. The VL53L0X can detect the "time of flight", or how long the light has taken to bounce back to the sensor. Since it uses a very narrow light source, it is good for determining distance of only the surface directly in front of it. Unlike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
